# Fritzing sketch protoboard (saved by Fritzing 1.0.1rc)
breadboards: 3

parts:
  SOM1 = Daisy Seed [chip_label=IC package="DIP (Dual Inline) [THT]"]
  U4 = POT [knob_status=50% package=alps_pot]
  U5 = POT [knob_status=50% package=alps_pot]
  U6 = POT [knob_status=50% package=alps_pot]
  U7 = POT [knob_status=50% package=alps_pot]
  U8 = POT [knob_status=50% package=alps_pot]
  S1 = Pushbutton [package="[THT]"]
  S2 = Pushbutton [package="[THT]"]
  U9 = POT [knob_status=50% package=alps_pot]
  U10 = POT [knob_status=50% package=alps_pot]
  U11 = POT [knob_status=50% package=alps_pot]
  U12 = POT [knob_status=50% package=alps_pot]
  U13 = POT [knob_status=50% package=alps_pot]
  S3 = Pushbutton [package="[THT]"]
  S4 = Pushbutton [package="[THT]"]
  U14 = POT [knob_status=50% package=alps_pot]
  U15 = POT [knob_status=50% package=alps_pot]
  U16 = POT [knob_status=50% package=alps_pot]
  U17 = 74HC4051 [package=so16]  # not connected
  U18 = MOC3031-M [package=dil06]  # not connected
  R1 = Resistor [tolerance=±5% resistance=220 package="0603 [SMD]"]  # not connected
  R2 = Resistor [tolerance=±5% resistance=220 package="0603 [SMD]"]  # not connected
  D1 = Rectifier Diode [part_number=1N4001 package="Melf DO-213 AB [SMD]"]  # not connected
  U19 = MIDI_CONN_FEMALE_SUPPORT [package=din_5_female_support]  # not connected
  U20 = 2.5mm Audio Jack [package=stereojack2.5mm_stereojack2.5mm]  # not connected

nets:
  N1: SOM1.pin_11, S3.Pin_1, S3.Pin_2
  N2: SOM1.pin_12, S4.Pin_1, S4.Pin_2
  N3: SOM1.pin_13, S2.Pin_1, S2.Pin_2
  N4: SOM1.pin_14, S1.Pin_1, S1.Pin_2
  N5: SOM1.pin_23, U14.S
  N6: SOM1.pin_24, U9.S
  N7: SOM1.pin_25, U10.S
  N8: SOM1.pin_26, U11.S
  N9: SOM1.pin_27, U12.S
  N10: SOM1.pin_28, U13.S
  N11: SOM1.pin_29, U7.S
  N12: SOM1.pin_30, U8.S
  N13: SOM1.pin_31, U6.S
  N14: SOM1.pin_32, U5.S
  N15: SOM1.pin_35, U4.S
  N16: SOM1.pin_38, U4.E, U5.E, U6.E, U7.E, U8.E, U9.E, U10.E, U11.E, U12.E, U13.E, U14.E, U15.E, U16.E
  N17: SOM1.pin_40, U4.A, U5.A, U7.A, U8.A, U9.A, U10.A, U12.A, U13.A, U14.A, U15.A, U16.A
  N18: S1.Pin_3, S1.Pin_4, S2.Pin_3, S2.Pin_4, S3.Pin_3, S3.Pin_4, S4.Pin_3, S4.Pin_4

custom parts:
  Daisy Seed: Daisy is an embedded platform for music. It features everything you need for creating high fidelity audio hardware devices. Just plug in a USB cable and start making sound! No soldering required.
